# Fritzing sketch ROV (saved by Fritzing 0.9.3b)
breadboards: 3

parts:
  Parça1 = Arduino Motor Shield
  M1 = DC Motor  # not connected
  M2 = DC Motor  # not connected
  M3 = DC Motor  # not connected
  M4 = DC Motor  # not connected
  Parça2 = Arduino Motor Shield
  Parça3 = Arduino Uno (Rev3) - ICSP  # not connected
  Parça4 = Arduino Uno (Rev3) - ICSP  # not connected
  J1 = Basic Servo
  Parça5 = Arduino Uno (Rev3) - ICSP
  U1 = TRANSCHIPTC5747 [package=camera_sfv24r-2st_2]
  Parça6 = Soil Moisture Sensor
  J2 = Infrared Proximity Sensor
  J3 = Infrared Proximity Sensor
  J4 = Basic Servo
  J5 = Basic Servo
  BAT1 = BC9VPC [package=bc9vpc]
  J6 = Basic Force Sensing Resistor (FSR) [package=THT]
  R1 = Resistor [tolerance=±5% resistance=220 package="2512 [SMD]"]
  R2 = Basic Flex Resistor
  R3 = Resistor [tolerance=±5% resistance=220 package="2512 [SMD]"]
  Parça7 = Arduino Esplora (Rev4)
  U2 = TMP36 [package=to-92-kit]

nets:
  N1: Parça1.OUT2, Parça1.OUT3, Parça2.OUT3, Parça2.OUT2, Parça7.5V
  N2: Parça1.OUT4, Parça1.OUT1, Parça2.OUT1, Parça2.OUT4, Parça7.GND
  N3: Parça1.A0, R3.Pin_0
  3.3V: Parça2.3.3V, J4.vcc
  5V: Parça2.5V, J1.vcc
  N4: Parça2.A0, J1.pulse
  N5: Parça2.A1, J4.pulse
  N6: Parça2.A2, J5.pulse
  GND: Parça2.GND, J1.gnd, J4.gnd
  N7: Parça5.A1, J6.pin_1, R1.Pin_0
  N8: Parça5.A2, U2.VOUT
  GND_2: Parça5.GND, U1.DOUT_5, Parça6.GND, J3.GND, BAT1.V-, U2.GND
  N9: Parça5.D3_PWM, J3.Vout
  N10: Parça5.D4, J2.Vout
  N11: Parça5.D5_PWM, Parça6.SIG
  N12: Parça5.D6_PWM, U1.DOUT_2
  N13: Parça5.D7, U1.DOUT_3
  3V3: Parça5.3V3, J3.Vcc
  5V_2: Parça5.5V, U1.DOUT_4, J6.pin_0, U2.VCC
  VIN: Parça5.VIN, Parça6.VCC, BAT1.V+
  N14: R2.Pin_2, R3.Pin_1
